# Fritzing sketch morseduino (saved by Fritzing 0.9.3b)
breadboards: 1

parts:
  R1 = Resistor [tolerance=±5% resistance=10k package=THT]
  J1 = Piezo Speaker
  Part1 = Arduino Uno (Rev3)
  S2 = Toggle Switch [package=THT]
  R2 = Resistor [tolerance=±5% resistance=10k package=THT]
  R3 = Resistor [tolerance=±5% resistance=100 package=THT]
  S3 = Round Pushbutton
  C2 = Ceramic Capacitor [capacitance="100 nF" package="0603 [SMD, multilayer]"]
  C1 = Ceramic Capacitor [capacitance="100 nF" package="0603 [SMD, multilayer]"]

nets:
  N1: R1.Pin_0, Part1.D2, S3.leg1, C2.1, C1.0
  N2: J1.pin1, Part1.GND, S2.COM, R2.Pin_1
  N3: J1.pin2, R3.Pin_0
  N4: Part1.D8, R3.Pin_1
  N5: Part1.D4, S2.L1
  N6: S2.L2, R2.Pin_0
  N7: C2.0, C1.1

notes:
  Connect the Morse key in place of this push button =>
  <= Mode selection switch

// code stored in the sketch: morseduino.ino

const String CONST_STRING = "cq cq cq 4s7kg";

const int tonePin = 8;      // output audio on pin 8
const int keyPin = 2;       // Morse key pin
const int switchModePin = 4; // Pin for switching between Morse key input and serial input
const int note = 1800;      // music note/pitch

const char MORSE_A[] = "._";
const char MORSE_B[] = "_...";
const char MORSE_C[] = "_._.";
const char MORSE_D[] = "_..";
const char MORSE_E[] = ".";
const char MORSE_F[] = ".._.";
const char MORSE_G[] = "__.";
const char MORSE_H[] = "....";
const char MORSE_I[] = "..";
const char MORSE_J[] = ".___";
const char MORSE_K[] = "_._";
const char MORSE_L[] = "._..";
const char MORSE_M[] = "__";
const char MORSE_N[] = "_.";
const char MORSE_O[] = "___";
const char MORSE_P[] = ".__.";
const char MORSE_Q[] = "__._";
const char MORSE_R[] = "._.";
const char MORSE_S[] = "...";
const char MORSE_T[] = "_";
const char MORSE_U[] = "_.";
const char MORSE_V[] = "..._";
const char MORSE_W[] = ".__";
const char MORSE_X[] = "_.._";
const char MORSE_Y[] = "_.__";
const char MORSE_Z[] = "__..";
const char MORSE_1[] = ".____";
const char MORSE_2[] = "..___";
const char MORSE_3[] = "...__";
const char MORSE_4[] = "...._";
const char MORSE_5[] = ".....";
const char MORSE_6[] = "_....";
const char MORSE_7[] = "__...";
const char MORSE_8[] = "___..";
const char MORSE_9[] = "____.";
const char MORSE_0[] = "_____";
const char MORSE_PERIOD[] = "._._._";
const char MORSE_COMMA[] = "__..__";
const char MORSE_QUESTION_MARK[] = "..__..";
const char MORSE_SOS[] = "...___...";
const char MORSE_KA[] = "_._._";

/*
  Set the speed of your morse code
  Adjust the 'dotlen' length to speed up or slow down your morse code
    (all of the other lengths are based on the dotlen)

  Here are the ratios code elements:
    Dash length = Dot length x 3
    Pause between elements = Dot length
      (pause between dots and dashes within the character)
    Pause between characters = Dot length x 3
    Pause between words = Dot length x 7
*/
const int dotLen = 80;     // length of the morse code 'dot'
const int dashLen = dotLen * 3;    // length of the morse code 'dash'
const int elemPause = dotLen;  // length of the pause between elements of a character
const int charSpacing = dotLen * 4;     // length of the spaces between characters
const int wordSpacing = dotLen * 7;  // length of the pause between words

const int MODE_PLAY_CODED_STRING = 0;
const int MODE_READ_FROM_SERIAL = 1;
const int MODE_OSCILLATOR = 2;

int mode = MODE_PLAY_CODED_STRING;
// int mode = MODE_READ_FROM_SERIAL;
// int mode = MODE_OSCILLATOR;

int morseKeyState;             // the current reading from the input pin
int lastMorseKeyState = LOW;   // the previous reading from the input pin
// the following variables are unsigned longs because the time, measured in
// milliseconds, will quickly become a bigger number than can be stored in an int.
unsigned long lastDebounceTime = 0;  // the last time the output pin was toggled
unsigned long debounceDelay = 25;    // the debounce time; increase if the output flickers

// the setup routine runs once when you press reset:
void setup() {
  pinMode(keyPin, INPUT);
  pinMode(switchModePin, INPUT);
  Serial.begin(9600);
}

void loop() {
  int mode = (digitalRead(switchModePin) == HIGH) ? MODE_READ_FROM_SERIAL : MODE_OSCILLATOR;
  switch (mode) {
    case MODE_PLAY_CODED_STRING:
      playCode(CONST_STRING);
      break;
    case MODE_READ_FROM_SERIAL:
      playCodeFromSerial();
      break;
    case MODE_OSCILLATOR:
      playOscillator();
      break;
    default:
      break;
  }
}

// The time at which a dot or dash started. This is used for identifying dots and dashes
int symbolStartedAt = -1;

// The time at which the last dot or dash was received. This is used to identify character boundaries.
int lastSymbolReceivedAt = -1;

// The time at which the last character was received. This is used for identifying word boundaries.
int lastCharReceivedAt = -1;

// Holds the currently active symbol (dots and dashes) buffer.
// This will be used later for identifying the character from the dots and dashes.
const int MAX_SYMBOLS = 7;
char currentSymbolBuff[MAX_SYMBOLS]; // Maximum possible symbols in Morse code is 6
int currentSymbolIndex = 0; // index to the currentSymbolBuff
bool garbageReceived = false; // Indicates whether the received symbol sequence is invalid

void playOscillator() {
  int reading = digitalRead(keyPin);
  // If the switch changed, due to noise or pressing:
  if (reading != lastMorseKeyState) {
    // reset the debouncing timer
    lastDebounceTime = millis();
  }

  // whatever the reading is at, it's been there for longer than the debounce
  // delay, so take it as the actual current state:
  // AND
  // if the button state has changed:
  if ((millis() - lastDebounceTime) > debounceDelay && reading != morseKeyState) {
    morseKeyState = reading;
    if (morseKeyState == HIGH) {
      int now = millis();
      if (symbolStartedAt == -1) {
        symbolStartedAt = now;
      }
      tone(tonePin, note);
    } else {
      noTone(tonePin);
      if (symbolStartedAt != -1) {
        if (currentSymbolIndex > MAX_SYMBOLS) {
          garbageReceived = true;
        } else if (!garbageReceived) {
          int now = millis();
          if (now - symbolStartedAt >= dashLen) {
            //            Serial.print("_");
            currentSymbolBuff[currentSymbolIndex++] = '_';
          } else {
            //            Serial.print(".");
            currentSymbolBuff[currentSymbolIndex++] = '.';
          }
          symbolStartedAt = -1;
          lastSymbolReceivedAt = millis();
          lastCharReceivedAt = -1;
        }
      }
    }
  }
  if (morseKeyState == LOW) {
    int now = millis();
    if (lastCharReceivedAt != -1 && now - lastCharReceivedAt > wordSpacing) {
      Serial.print(" ");
      lastCharReceivedAt = -1;
    } else if (lastSymbolReceivedAt != -1 && now - lastSymbolReceivedAt > charSpacing) {
      Serial.print(morseToChar(currentSymbolBuff));
      garbageReceived = false;
      resetCurrentSymbolBuff();
      lastSymbolReceivedAt = -1;
      lastCharReceivedAt = millis();
    }
  }
  // save the reading. Next time through the loop, it'll be the lastMorseKeyState:
  lastMorseKeyState = reading;
}

void resetCurrentSymbolBuff() {
  for (int i = 0; i < MAX_SYMBOLS; i++) {
    currentSymbolBuff[i] = '\0';
  }
  currentSymbolIndex = 0;
}

void playCodeFromSerial() {
  if (Serial.available() > 0) {
    String serialRead = Serial.readString();
    playCode(serialRead);
  }
}

void playCode(String strToPlay) {
  char str[strToPlay.length() + 1] ;
  strToPlay.toCharArray(str, strToPlay.length() + 1);
  for (int i = 0; i < sizeof(str) - 1; i++) {
    playMorse(toLowerCase(str[i]));
    delay(dotLen * 2);
    Serial.print(str[i]);
  }
  Serial.println();
  pause(5000);
}

void di() {
  tone(tonePin, note, dotLen);
  delay(dotLen);
  pause(elemPause);
}

void dah() {
  tone(tonePin, note, dashLen);  // start playing a tone
  delay(dashLen);               // hold in this position
  pause(elemPause);
}

void pause(int delayTime) {
  noTone(tonePin);
  delay(delayTime);
}

void playMorseSequence(String morseSequence) {
  char morseCharSeq[morseSequence.length() + 1] ;
  morseSequence.toCharArray(morseCharSeq, morseSequence.length() + 1);
  for (int i = 0; i < sizeof(morseCharSeq) - 1; i++) {
    morseCharSeq[i] == '.' ? di() : dah();
  }
}

int lengthof(char const str[]) {
  int i = 0;
  while (str[i] != '\0') {
    i++;
  }
  return i;
}

bool isEqual(char ch1[], char const ch2[]) {
  if (lengthof(ch1) != lengthof(ch2)) return false;
  int i = 0;
  while (ch1[i] != '\0' && ch2[i] != '\0') {
    if (ch1[i] != ch2[i]) return false;
    i++;
  }
  return true;
}

char morseToChar(char morseStr[]) {
  if (isEqual(morseStr, MORSE_A)) {
    return 'a';
  } else if (isEqual(morseStr, MORSE_B)) {
    return 'b';
  } else if (isEqual(morseStr, MORSE_C)) {
    return 'c';
  } else if (isEqual(morseStr, MORSE_D)) {
    return 'd';
  } else if (isEqual(morseStr, MORSE_E)) {
    return 'e';
  } else if (isEqual(morseStr, MORSE_F)) {
    return 'f';
  } else if (isEqual(morseStr, MORSE_G)) {
    return 'g';
  } else if (isEqual(morseStr, MORSE_H)) {
    return 'h';
  } else if (isEqual(morseStr, MORSE_I)) {
    return 'i';
  } else if (isEqual(morseStr, MORSE_J)) {
    return 'j';
  } else if (isEqual(morseStr, MORSE_K)) {
    return 'k';
  } else if (isEqual(morseStr, MORSE_L)) {
    return 'l';
  } else if (isEqual(morseStr, MORSE_M)) {
    return 'm';
  } else if (isEqual(morseStr, MORSE_N)) {
    return 'n';
  } else if (isEqual(morseStr, MORSE_O)) {
    return 'o';
  } else if (isEqual(morseStr, MORSE_P)) {
    return 'p';
  } else if (isEqual(morseStr, MORSE_Q)) {
    return 'q';
  } else if (isEqual(morseStr, MORSE_R)) {
    return 'r';
  } else if (isEqual(morseStr, MORSE_S)) {
    return 's';
  } else if (isEqual(morseStr, MORSE_T)) {
    return 't';
  } else if (isEqual(morseStr, MORSE_U)) {
    return 'u';
  } else if (isEqual(morseStr, MORSE_V)) {
    return 'v';
  } else if (isEqual(morseStr, MORSE_W)) {
    return 'w';
  } else if (isEqual(morseStr, MORSE_X)) {
    return 'x';
  } else if (isEqual(morseStr, MORSE_Y)) {
    return 'y';
  } else if (isEqual(morseStr, MORSE_Z)) {
    return 'z';
  } else if (isEqual(morseStr, MORSE_1)) {
    return '1';
  } else if (isEqual(morseStr, MORSE_2)) {
    return '2';
  } else if (isEqual(morseStr, MORSE_3)) {
    return '3';
  } else if (isEqual(morseStr, MORSE_4)) {
    return '4';
  } else if (isEqual(morseStr, MORSE_5)) {
    return '5';
  } else if (isEqual(morseStr, MORSE_6)) {
    return '6';
  } else if (isEqual(morseStr, MORSE_7)) {
    return '7';
  } else if (isEqual(morseStr, MORSE_8)) {
    return '8';
  } else if (isEqual(morseStr, MORSE_9)) {
    return '9';
  } else if (isEqual(morseStr, MORSE_0)) {
    return '0';
  } else if (isEqual(morseStr, MORSE_PERIOD)) {
    return '.';
  } else if (isEqual(morseStr, MORSE_COMMA)) {
    return ',';
  } else if (isEqual(morseStr, MORSE_QUESTION_MARK)) {
    return '?';
  } else if (isEqual(morseStr, MORSE_KA)) {
    return '>';
  } else if (garbageReceived) {
    return '#';
  } else {
    //    Serial.println();
    //    Serial.println(morseStr);
    return '#';
  }
}

void playMorse(char normalChar) {
  switch (normalChar) {
    case 'a':
      playMorseSequence(MORSE_A);
      break;
    case 'b':
      playMorseSequence(MORSE_B);
      break;
    case 'c':
      playMorseSequence(MORSE_C);
      break;
    case 'd':
      playMorseSequence(MORSE_D);
      break;
    case 'e':
      playMorseSequence(MORSE_E);
      break;
    case 'f':
      playMorseSequence(MORSE_F);
      break;
    case 'g':
      playMorseSequence(MORSE_G);
      break;
    case 'h':
      playMorseSequence(MORSE_H);
      break;
    case 'i':
      playMorseSequence(MORSE_I);
      break;
    case 'j':
      playMorseSequence(MORSE_J);
      break;
    case 'k':
      playMorseSequence(MORSE_K);
      break;
    case 'l':
      playMorseSequence(MORSE_L);
      break;
    case 'm':
      playMorseSequence(MORSE_M);
      break;
    case 'n':
      playMorseSequence(MORSE_N);
      break;
    case 'o':
      playMorseSequence(MORSE_O);
      break;
    case 'p':
      playMorseSequence(MORSE_P);
      break;
    case 'q':
      playMorseSequence(MORSE_Q);
      break;
    case 'r':
      playMorseSequence(MORSE_R);
      break;
    case 's':
      playMorseSequence(MORSE_S);
      break;
    case 't':
      playMorseSequence(MORSE_T);
      break;
    case 'u':
      playMorseSequence(MORSE_U);
      break;
    case 'v':
      playMorseSequence(MORSE_V);
      break;
    case 'w':
      playMorseSequence(MORSE_W);
      break;
    case 'x':
      playMorseSequence(MORSE_X);
      break;
    case 'y':
      playMorseSequence(MORSE_Y);
      break;
    case 'z':
      playMorseSequence(MORSE_Z);
      break;
    case '1':
      playMorseSequence(MORSE_1);
      break;
    case '2':
      playMorseSequence(MORSE_2);
      break;
    case '3':
      playMorseSequence(MORSE_3);
      break;
    case '4':
      playMorseSequence(MORSE_4);
      break;
    case '5':
      playMorseSequence(MORSE_5);
      break;
    case '6':
      playMorseSequence(MORSE_6);
      break;
    case '7':
      playMorseSequence(MORSE_7);
      break;
    case '8':
      playMorseSequence(MORSE_8);
      break;
    case '9':
      playMorseSequence(MORSE_9);
      break;
    case '0':
      playMorseSequence(MORSE_0);
      break;
    case '.':
      playMorseSequence(MORSE_PERIOD);
      break;
    case ',':
      playMorseSequence(MORSE_COMMA);
      break;
    case '?':
      playMorseSequence(MORSE_QUESTION_MARK);
      break;
    case ' ':
      pause(wordSpacing);
      break;
    default:
      pause(charSpacing);
  }
}
